# Fritzing sketch Esquema (saved by Fritzing 0.9.2b)
breadboards: 1

parts:
  Parte2 = Arduino Uno (Rev3)
  LED2 = LED - 5mm [color="Red (633nm)" package="5 mm [THT]"]
  R3 = Resistor [tolerance=±5% resistance=1k package=THT]
  T1 = LM35 Temperature Sensor [package="TO92 [THT]"]

nets:
  N1: Parte2.A0, T1.Vout
  N2: Parte2.D4, LED2.anode
  N3: Parte2.5V, T1.+Vs
  GND: Parte2.GND, R3.Pin_0, T1.GND
  N4: LED2.cathode, R3.Pin_1
